# Fritzing sketch Ultrasonic_Instrument (saved by Fritzing 0.7.12b)
breadboards: 1
perfboards: 1

parts:
  Arduino2 = Arduino
  U2 = 74HC595 [package="DIP16 [THT]"]
  U3 = 74HC595 [package="DIP16 [THT]"]
  U4 = atmega328 [package=dip]
  LED1 = LED - 5mm [color="Blue (430nm)" package="5 mm [THT]"]
  LED7 = LED - 5mm [color="White (8000K)" package="5 mm [THT]"]
  LED8 = LED - 5mm [color="White (8000K)" package="5 mm [THT]"]
  LED9 = LED - 5mm [color="Blue (430nm)" package="5 mm [THT]"]
  LED10 = LED - 5mm [color="White (8000K)" package="5 mm [THT]"]
  LED11 = LED - 5mm [color="Blue (430nm)" package="5 mm [THT]"]
  LED12 = LED - 5mm [color="White (8000K)" package="5 mm [THT]"]
  LED13 = LED - 5mm [color="Blue (430nm)" package="5 mm [THT]"]
  LED14 = LED - 5mm [color="Blue (430nm)" package="5 mm [THT]"]
  LED15 = LED - 5mm [color="White (8000K)" package="5 mm [THT]"]
  LED16 = LED - 5mm [color="Blue (430nm)" package="5 mm [THT]"]
  LED17 = LED - 5mm [color="White (8000K)" package="5 mm [THT]"]
  LED18 = LED - 5mm [color="Blue (430nm)" package="5 mm [THT]"]
  LED19 = LED - 5mm [color="White (8000K)" package="5 mm [THT]"]
  LED20 = LED - 5mm [color="Blue (430nm)" package="5 mm [THT]"]
  LED21 = LED - 5mm [color="White (8000K)" package="5 mm [THT]"]
  R1 = Resistor [tolerance=±5% resistance=220 package=THT]
  U5 = Voltage Regulator - 5V [package="TO220 [THT]"]
  C1 = Electrolytic Capacitor [capacitance=10µF package="100 mil [THT, electrolytic]"]
  C2 = Electrolytic Capacitor [capacitance=10µF package="100 mil [THT, electrolytic]"]
  SPKR1 = Loudspeaker
  S1 = Pushbutton [package="[THT]"]
  S2 = Pushbutton [package="[THT]"]
  R2 = Resistor [tolerance=±5% resistance=220 package=THT]
  Part1 = SRF05 Ultrasonic Rangefinder
  LED22 = LED - 5mm [color="Red (633nm)" package="5 mm [THT]"]
  RE2 = Rotary Encoder [package=THT]
  R4 = Resistor [tolerance=±5% resistance=220 package=THT]
  R5 = Resistor [tolerance=±5% resistance=220 package=THT]
  XTAL1 = Crystal [frequency="16 Mhz" package=SMD]
  R6 = Resistor [tolerance=±5% resistance=220 package=THT]
  R7 = Resistor [tolerance=±5% resistance=220 package=THT]
  Power_plug1 = Power plug
  RE3 = Rotary Encoder [package=THT]
  S3 = Pushbutton [package="[THT]"]
  S4 = Pushbutton [package="[THT]"]
  Part2 = SRF05 Ultrasonic Rangefinder
  R8 = Resistor [tolerance=±5% resistance=220 package=THT]
  R9 = Resistor [tolerance=±5% resistance=220 package=THT]
  R10 = Resistor [tolerance=±5% resistance=220 package=THT]
  R11 = Resistor [tolerance=±5% resistance=220 package=THT]
  SPKR2 = Loudspeaker
  LED23 = LED - 5mm [color="Red (633nm)" package="5 mm [THT]"]
  R12 = Resistor [tolerance=±5% resistance=220 package=THT]
  R13 = Resistor [tolerance=±5% resistance=220 package=THT]
  R14 = Resistor [tolerance=±5% resistance=220 package=THT]

nets:
  N1: Arduino2.D12, U2.SH_CP
  N2: Arduino2.D11, U2.DS
  N3: Arduino2.D9, SPKR2.pin2
  N4: Arduino2.D8, U2.ST_CP
  N5: Arduino2.D7, S3.Pin_1, S3.Pin_2, R13.Pin_1
  N6: Arduino2.D6, S4.Pin_1, S4.Pin_2, R14.Pin_1
  N7: Arduino2.D5, LED23.anode
  N8: Arduino2.D4, Part2.Echo
  N9: Arduino2.D3, Part2.Trig
  N10: Arduino2.D2, R11.Pin_0
  N11: Arduino2.D1TX, RE3.EncoderPinA, R8.Pin_0
  N12: Arduino2.D0RX, RE3.EncoderPinB, R9.Pin_0
  VCC: Arduino2.+5V, U2.MR, U2.VCC, S3.Pin_3, S3.Pin_4, S4.Pin_3, S4.Pin_4, Part2.VCC, R8.Pin_1, R9.Pin_1
  GND: Arduino2.GND, U2.OE, RE3.EncoderPinC, Part2.GND, R10.Pin_1, R11.Pin_1, SPKR2.pin1, R12.Pin_0, R13.Pin_0, R14.Pin_0
  N13: U2.Q1, LED7.anode
  N14: U2.Q2, LED9.anode
  N15: U2.Q3, LED8.anode
  N16: U2.Q4, LED11.anode
  N17: U2.Q5, LED10.anode
  N18: U2.Q6, LED13.anode
  N19: U2.Q7, LED12.anode
  N20: U2.Q0, LED1.anode
  N21: U3.Q1, LED15.anode
  N22: U3.Q2, LED16.anode
  N23: U3.Q3, LED17.anode
  N24: U3.Q4, LED18.anode
  N25: U3.Q5, LED19.anode
  N26: U3.Q6, LED20.anode
  N27: U3.Q7, LED21.anode
  GND_2: U3.GND, U3.OE, U4.GND#21, LED14.cathode, R1.Pin_1, U5.GND, C1.-, C2.-, SPKR1.pin1, R2.Pin_0, Part1.GND, LED22.cathode, R4.Pin_1, R5.Pin_0, Power_plug1.GND
  VCC_2: U3.MR, U3.VCC, U4.VCC, U4.AVCC, U4.AREF, U5.output_voltage, C1.+, S1.Pin_3, S1.Pin_4, S2.Pin_3, S2.Pin_4, Part1.VCC, R6.Pin_1, R7.Pin_0
  N28: U3.SH_CP, U4.D12
  N29: U3.ST_CP, U4.D8
  N30: U3.DS, U4.D11_(PWM)
  N31: U3.Q0, LED14.anode
  N32: U4.D0_(RX), RE2.EncoderPinB, R6.Pin_0
  N33: U4.D1_(TX), RE2.EncoderPinA, R7.Pin_1
  N34: U4.D2, Part1.Echo
  N35: U4.D3_(PWM), Part1.Trig
  N36: U4.D4, S2.Pin_1, S2.Pin_2, R5.Pin_1
  N37: U4.XLAT1, XTAL1.pin_1
  N38: U4.XLAT2, XTAL1.pin_0
  N39: U4.D6_(PWM), R4.Pin_0
  N40: U4.D7, S1.Pin_1, S1.Pin_2, R2.Pin_1
  N41: U4.D9_(PWM), SPKR1.pin2
  N42: LED1.cathode, LED7.cathode, LED8.cathode, LED9.cathode, LED10.cathode, LED11.cathode, LED12.cathode, LED13.cathode, R10.Pin_0
  N43: LED19.cathode, LED20.cathode, LED21.cathode, R1.Pin_0
  N44: U5.input_voltage, Power_plug1.VCC
  N45: LED23.cathode, R12.Pin_1
